# Fritzing sketch EEPROM_ESP8266_ServoMotor (saved by Fritzing 0.9.3b)
breadboards: 1

parts:
  Amica_NodeMCU_DevKit_1_1 = Amica NodeMCU DevKit 1.0
  J1 = Basic Servo

nets:
  N1: Amica_NodeMCU_DevKit_1_1.pin8, J1.pulse
  N2: Amica_NodeMCU_DevKit_1_1.pin_25, Amica_NodeMCU_DevKit_1_1.pin_29, J1.gnd
  N3: Amica_NodeMCU_DevKit_1_1.pin_30, J1.vcc

custom parts:
  Amica NodeMCU DevKit 1.0: Amica NodeMCU DEVKIT 1.0 Development Kit based on ESP8266 ESP-12E, integating GPIO, PWM, IIC, 1-Wire and ADC all in one board.
